// Logisim project cl2e2_jessop.circ as structural Verilog: 1 circuit, main circuit main
module main (
  input  A,
  input  B,
  input  C,
  input  D,
  output Output
);

  wire and_1_out, and_2_out, not_1_out, not_2_out;

  not not_1 (not_1_out, C);
  and and_1 (and_1_out, B, not_1_out);
  not not_2 (not_2_out, A);
  and and_2 (and_2_out, not_2_out, B, D);
  or or_1 (Output, and_2_out, and_1_out);

  // Notes on the sheet:
  //   Inputs
endmodule
