// Logisim project sle2_jessop.circ as structural Verilog: 1 circuit, main circuit main
module main (
  input  in_1,
  output Output
);

  wire and_1_out, and_2_out, and_3_out, and_4_out, and_5_out, clock_1_out, d_ff_1_q, d_ff_1_qn, d_ff_2_q,
       d_ff_2_qn, or_1_out, or_2_out;

  Clock clock_1 (.out(clock_1_out));
  and and_1 (and_1_out, in_1, or_2_out);
  and and_2 (and_2_out, in_1, or_1_out);
  D_Flip_Flop #(.trigger("falling")) d_ff_1 (
    .clk(clock_1_out), .D(and_1_out), .Q(d_ff_1_q), .Qn(d_ff_1_qn));  // open: preset, en, reset
  D_Flip_Flop #(.trigger("falling")) d_ff_2 (
    .clk(clock_1_out), .D(and_2_out), .Q(d_ff_2_q), .Qn(d_ff_2_qn));  // open: preset, en, reset
  or or_1 (or_1_out, d_ff_2_qn, and_5_out);
  and and_3 (and_3_out, d_ff_1_q, d_ff_2_qn);
  or or_2 (or_2_out, and_3_out, and_4_out, and_5_out);
  and and_4 (and_4_out, d_ff_1_qn, d_ff_2_q);
  and and_5 (and_5_out, d_ff_2_q, d_ff_1_q);
  and and_6 (Output, d_ff_1_q, d_ff_2_q);

  // Notes on the sheet:
  //   Input
endmodule
